// Logisim project projetofinal.circ as structural Verilog: 14 circuits, main circuit main
module main (
);

  wire A_JOGANDO, A_VENCEU, and_1_out, and_2_out, and_3_out, and_4_out, and_7_out, and_8_out, and_9_out,
       \AVANÇAR_A , \AVANÇAR_B , B_JOGANDO, B_VENCEU, C_A, C_B, clok, clok1, comparator_1_eq,
       comparator_2_eq, comparator_2_gt, comparator_2_lt, \config , core_1_fim_a, core_1_fim_b,
       core_1_jogando_a, core_1_x_jogando, counter_1_carry, counter_2_carry, e_out, EMPATE, fim_out, FINAL,
       iniciar, Min1, Min2, or_1_out, or_2_out, or_3_out, plus_A, plus_B, \PRÓXIMO_N , reset, rgbled_1_p4,
       Seg1, Seg2, SOMA_CERTA, T_O, T_O_2, X__CERTO, X_JOGANDO, Y__CERTO, Y_JOGANDO;
  wire [1:0] counter_1_q;
  wire [3:0] bPM1, bPM2, bPS1, bPS2, PALPITE_A, PALPITE_B, PM1, PM2, PONTO_A, PONTO_B, PS1, PS2, X_ATUAL,
       Y_ATUAL;
  wire [7:0] A, V;

  Hex_Digit_Display hex_digit_display_1 (.value(PM1));  // open: dp
  Hex_Digit_Display hex_digit_display_2 (.value(PM2));  // open: dp
  Button button_1 (.out(plus_A));
  \temp_m_s__botão  \temp_m_s__botão_1  (
    .play(iniciar), .clk(and_1_out), ._2bm(Min2), ._1bm(Min1), ._2bs(Seg2), .in_7(Seg1), .reset(reset),
    .out_8(PM2), .out_9(PM1), .out_10(PS2), .out_11(PS1), .fim(T_O), .Config(\config ));
  Hex_Digit_Display hex_digit_display_3 (.value(PONTO_A));  // open: dp
  Hex_Digit_Display hex_digit_display_4 (.value(PS2));  // open: dp
  Hex_Digit_Display hex_digit_display_5 (.value(PALPITE_A));  // open: dp
  Button button_2 (.out(C_A));
  Button button_3 (.out(\AVANÇAR_A ));
  LED led_1 (.in(A_JOGANDO));
  and and_1 (and_1_out, clok, ~T_O);  // AND_Gate
  Hex_Digit_Display hex_digit_display_6 (.value(PS1));  // open: dp
  LED led_2 (.in(A_VENCEU));
  LED led_3 (.in(X__CERTO));
  LED led_4 (.in(SOMA_CERTA));
  Hex_Digit_Display hex_digit_display_7 (.value(X_ATUAL));  // open: dp
  LED led_5 (.in(X_JOGANDO));
  Button button_4 (.out(Min1));
  Button button_5 (.out(Min2));
  Button button_6 (.out(iniciar));
  Alternar_jogador alternar_jogador_1 (.clk(clok), .clh1(clok1), .troca(comparator_1_eq));
  Counter #(.width(2), .max('h2), .trigger("falling")) counter_1 (
    .Q(counter_1_q), .carry(counter_1_carry), .clk(or_1_out), .clr(counter_1_carry));  // open: load, D, count, preset, down
  or or_1 (or_1_out, \AVANÇAR_A , \AVANÇAR_B );
  LED led_6 (.in(FINAL));
  LED led_7 (.in(EMPATE));
  Hex_Digit_Display hex_digit_display_8 (.value(Y_ATUAL));  // open: dp
  LED led_8 (.in(Y_JOGANDO));
  LED led_9 (.in(\config ));
  Button button_7 (.out(Seg2));
  Comparator #(.width(2)) comparator_1 (.a(counter_1_q), .b(2'b10), .eq(comparator_1_eq));  // open: gt, lt
  LED led_10 (.in(B_VENCEU));
  // RGBLed #(.multibit("true")) rgbled_1: pin names not known; wires that end beside it: SOMA_CERTA, V, A, rgbled_1_p4
  LED led_11 (.in(Y__CERTO));
  Button button_8 (.out(Seg1));
  Button button_9 (.out(reset));
  \temp_m_s__botão  \temp_m_s__botão_2  (
    .play(iniciar), .clk(and_2_out), ._2bm(Min2), ._1bm(Min1), ._2bs(Seg2), .in_7(Seg1), .reset(reset),
    .out_8(bPM2), .out_9(bPM1), .out_10(bPS2), .out_11(bPS1), .fim(T_O_2));  // open: Config
  and and_2 (and_2_out, clok1, ~T_O_2);  // AND_Gate
  Hex_Digit_Display hex_digit_display_9 (.value(bPM2));  // open: dp
  Hex_Digit_Display hex_digit_display_10 (.value(bPM1));  // open: dp
  Button button_10 (.out(plus_B));
  Hex_Digit_Display hex_digit_display_11 (.value(PONTO_B));  // open: dp
  Hex_Digit_Display hex_digit_display_12 (.value(bPS2));  // open: dp
  Hex_Digit_Display hex_digit_display_13 (.value(PALPITE_B));  // open: dp
  Button button_11 (.out(C_B));
  LED led_12 (.in(B_JOGANDO));
  Hex_Digit_Display hex_digit_display_14 (.value(bPS1));  // open: dp
  Button button_12 (.out(\AVANÇAR_B ));
  and and_3 (and_3_out, ~T_O, plus_A);  // AND_Gate
  and and_4 (and_4_out, ~T_O_2, plus_B);  // AND_Gate
  or or_2 (or_2_out, reset, \PRÓXIMO_N , iniciar);
  and and_5 (X_JOGANDO, ~\config , core_1_x_jogando);  // AND_Gate
  and and_6 (A_JOGANDO, ~\config , core_1_jogando_a);  // AND_Gate
  core core_1 (
    .NOVO_N(or_2_out), .A(and_3_out), .C_A(C_A), .AVAN_A(\AVANÇAR_A ), .B(and_4_out), .C_B(C_B),
    .AVAN_B(\AVANÇAR_B ), .PONTO_A(PONTO_A), .X_CERTO(X__CERTO), .Y_CERTO(Y__CERTO), .PONTO_B(PONTO_B),
    .X_ATUAL(X_ATUAL), .Y_ATUAL(Y_ATUAL), .X_JOGANDO(core_1_x_jogando), .Y_JOGANDO(Y_JOGANDO),
    .JOGANDO_A(core_1_jogando_a), .AZUL(A), .VERMELHO(V), .SOMA_CERTA(SOMA_CERTA), .FIM_A(core_1_fim_a),
    .PALPITE_A(PALPITE_A), .JOGANDO_B(B_JOGANDO), .PALPITE_B(PALPITE_B), .RESET(reset), .FIM_B(core_1_fim_b));
  and and_7 (and_7_out, X__CERTO, Y__CERTO);
  or or_3 (or_3_out, \AVANÇAR_A , \AVANÇAR_B );
  Counter #(.width(1), .max('h1)) counter_2 (
    .Q(\PRÓXIMO_N ), .carry(counter_2_carry), .clk(and_8_out), .clr(counter_2_carry));  // open: load, D, count, preset, down
  and and_8 (and_8_out, and_7_out, or_3_out);
  and and_9 (and_9_out, T_O_2, T_O);
  or fim (fim_out, and_9_out, core_1_fim_a, core_1_fim_b);
  Comparator #(.width(4)) comparator_2 (
    .a(PONTO_A), .b(PONTO_B), .gt(comparator_2_gt), .eq(comparator_2_eq), .lt(comparator_2_lt));
  and and_10 (FINAL, ~\config , fim_out);  // AND_Gate
  and av (A_VENCEU, fim_out, comparator_2_gt);
  and and_11 (EMPATE, ~\config , e_out);  // AND_Gate
  and e (e_out, fim_out, comparator_2_eq);
  and bv (B_VENCEU, fim_out, comparator_2_lt);

  // Notes on the sheet:
  //   JOGADOR A
  //   PLACAR
  //   CRONÔMETRO
  //   .
  //   .
  //   PALPITE
  //   +
  //   JOGADOR B
  //   PLACAR
  //   CRONÔMETRO
  //   .
  //   .
  //   PALPITE
  //   PASSOS PARA JOGAR
  //   1. Defina o tempo nos botões;
  //   INFORMAÇÕES GERAIS
  //   2. Lique o clock(ctrl+K) e aperte em iniciar;
  //   3. Jogador A chuta o x, confirma e avança para o Y;
  //   5. Jogador B chuta o X, confirma e avança para o Y;
  //   Quando algum dos jogadores chegar a 4 pontos, este vence.
  //   Quando o tempo de ambos acabar teremos empate.
  //   a cada chute do jogador que ainda possui tempo.
  //   4. Jogador A chuta o y, confirma e avança para a vez do Jogador B;
  //   6. Jogador B chuta o Y, confirma e avança para a vez do Jogador A;
  //   7. Os jogadores revesam até algum ganhar ou o tempo de ambos acabar. 
  //   Quando o tempo de apenas um jigador acabar o outro continuará jogando,
  //   precisando que o jogador cujo tempo acabou clique em avaçar duas vezes
endmodule

module projeto_2__cronometro__modelo1 (
  input  in_1,
  output [3:0] out_2,
  output [3:0] out_3,
  output [3:0] out_4,
  output [3:0] out_5,
  output [3:0] out_6,
  output [3:0] out_7,
  output [3:0] out_8,
  output [3:0] out_9
);

  wire adder_1_out, and_1_out, and_2_out, and_3_out, and_4_out, and_5_out, and_6_out, clock_1_out,
       counter_2_carry, counter_3_carry, counter_4_carry, counter_6_carry, counter_7_carry, counter_8_carry,
       register_1_q;

  and and_1 (and_1_out, counter_2_carry, counter_3_carry, counter_4_carry);
  Counter #(.width(4), .max('h5)) counter_1 (
    .count(and_1_out), .Q(out_6), .clk(and_3_out), .down(1'b1));  // open: load, D, carry, clr, preset
  and and_2 (and_2_out, counter_4_carry, counter_3_carry);
  Counter #(.width(4), .max('h9)) counter_2 (
    .count(and_2_out), .Q(out_7), .carry(counter_2_carry), .clk(and_3_out), .down(1'b1));  // open: load, D, clr, preset
  and and_3 (and_3_out, clock_1_out, ~register_1_q);  // AND_Gate
  Clock clock_1 (.out(clock_1_out));
  Counter #(.width(4), .max('h5)) counter_3 (
    .count(counter_4_carry), .Q(out_8), .carry(counter_3_carry), .clk(and_3_out), .down(1'b1));  // open: load, D, clr, preset
  Counter #(.width(4), .max('h9)) counter_4 (
    .Q(out_9), .carry(counter_4_carry), .clk(and_3_out), .down(1'b1));  // open: load, D, count, clr, preset
  Adder #(.width(1)) adder_1 (.a(1'b1), .b(register_1_q), .out(adder_1_out));  // open: cin, cout
  Register #(.width(1), .Select("low")) register_1 (.D(adder_1_out), .Q(register_1_q), .clk(in_1));  // open: en, clr
  and and_4 (and_4_out, register_1_q, clock_1_out);
  and and_5 (and_5_out, counter_6_carry, counter_7_carry, counter_8_carry);
  Counter #(.width(4), .max('h9)) counter_5 (
    .count(and_5_out), .Q(out_2), .clk(and_4_out), .down(1'b1));  // open: load, D, carry, clr, preset
  and and_6 (and_6_out, counter_8_carry, counter_7_carry);
  Counter #(.width(4), .max('h9)) counter_6 (
    .count(and_6_out), .Q(out_3), .carry(counter_6_carry), .clk(and_4_out), .down(1'b1));  // open: load, D, clr, preset
  Counter #(.width(4), .max('h5)) counter_7 (
    .count(counter_8_carry), .Q(out_4), .carry(counter_7_carry), .clk(and_4_out), .down(1'b1));  // open: load, D, clr, preset
  Counter #(.width(4), .max('h9)) counter_8 (
    .Q(out_5), .carry(counter_8_carry), .clk(and_4_out), .down(1'b1));  // open: load, D, count, clr, preset
endmodule

module modelo_de_cronometro (
);

  wire alternar_jogador_1_p4, clok, clok1, fima, fimb, iniciar, Min1, Min2, reset, Seg1, Seg2;
  wire [3:0] ld1, ld1b, ld2, ld2b, ls1, ls1b, ls4, ls4b;

  Hex_Digit_Display hex_digit_display_1 (.value(ld1));  // open: dp
  Button button_1 (.out(Min2));
  \temp_m_s__botão  \temp_m_s__botão_1  (
    .play(iniciar), .clk(clok), ._2bm(Min2), ._1bm(Min1), ._2bs(Seg2), .in_7(Seg1), .reset(reset),
    .out_8(ld1b), .out_9(ld2b), .out_10(ls1b), .out_11(ls4b));  // open: fim, Config
  Hex_Digit_Display hex_digit_display_2 (.value(ld2));  // open: dp
  Button button_2 (.out(Min1));
  Button button_3 (.out(iniciar));
  Hex_Digit_Display hex_digit_display_3 (.value(ls1));  // open: dp
  Hex_Digit_Display hex_digit_display_4 (.value(ls4));  // open: dp
  Button button_4 (.out(Seg2));
  Button button_5 (.out(Seg1));
  // temp_m_s__botão temp_m_s__botão_2: pin names not known; wires that end beside it: iniciar, ld1, Min2, Min1, ld2, clok1, ls1, Seg2, ls4, Seg1, reset, fima
  // Alternar_jogador alternar_jogador_1: pin names not known; wires that end beside it: clok, fima, clok1, alternar_jogador_1_p4, fimb
  Button button_6 (.out(alternar_jogador_1_p4));
  Hex_Digit_Display hex_digit_display_5 (.value(ld1b));  // open: dp
  Hex_Digit_Display hex_digit_display_6 (.value(ld2b));  // open: dp
  Button button_7 (.out(reset));
  Hex_Digit_Display hex_digit_display_7 (.value(ls1b));  // open: dp
  Hex_Digit_Display hex_digit_display_8 (.value(ls4b));  // open: dp
endmodule

// CRONÔMETRO
module \temp_m_s__botão  (
  input  play,
  input  reset,
  input  clk,
  input  _2bm,
  input  _1bm,
  input  _2bs,
  input  in_7,
  output [3:0] out_8,
  output [3:0] out_9,
  output [3:0] out_10,
  output [3:0] out_11,
  output fim,
  output Config
);

  wire comparator_1_eq, comparator_2_eq, comparator_3_eq, comparator_4_eq, tempo_segundos_1_s1,
       tempo_segundos_1_s2;

  tempo_minutos tempo_minutos_1 (
    .bot2(_2bm), .bot1(_1bm), .mudar(Config), ._2(tempo_segundos_1_s2), ._1(tempo_segundos_1_s1),
    .out_8(out_8), .out_9(out_9), .clk(clk), .reset(reset));
  T_Flip_Flop t_ff_1 (.clk(play), .T(1'b1), .Qn(Config));  // open: Q, preset, reset
  tempo_segundos tempo_segundos_1 (
    .bot2(_2bs), .mudar(Config), .bot1(in_7), .s1(tempo_segundos_1_s1), .s2(tempo_segundos_1_s2), .clk(clk),
    .out_6(out_10), .out_7(out_11), .reset(reset));
  Comparator #(.width(4)) comparator_1 (.a(out_11), .b(4'b0000), .eq(comparator_1_eq));  // open: gt, lt
  Comparator #(.width(4)) comparator_2 (.a(out_10), .b(4'b0000), .eq(comparator_2_eq));  // open: gt, lt
  Comparator #(.width(4)) comparator_3 (.a(out_9), .b(4'b0000), .eq(comparator_3_eq));  // open: gt, lt
  Comparator #(.width(4)) comparator_4 (.a(out_8), .b(4'b0000), .eq(comparator_4_eq));  // open: gt, lt
  and and_1 (fim, comparator_1_eq, comparator_2_eq, comparator_3_eq, comparator_4_eq);

  // Other names for the same wires on the sheet: t[3:0] = out_8; t2[3:0] = out_9
endmodule

module tempo_segundos (
  input  reset,
  input  bot2,
  input  bot1,
  input  mudar,
  input  clk,
  output [3:0] out_6,
  output [3:0] out_7,
  output s2,
  output s1
);

  wire counter_1_carry, counter_2_carry, multiplexer_1_out, multiplexer_2_out, or_1_out;

  and and_1 (s2, counter_1_carry, counter_2_carry);
  and and_2 (s1, counter_1_carry, counter_2_carry);
  Counter #(.width(4), .max('h5)) counter_1 (
    .count(or_1_out), .Q(out_6), .carry(counter_1_carry), .clk(multiplexer_1_out), .clr(reset), .down(1'b1));  // open: load, D, preset
  Multiplexer #(.enable("false")) multiplexer_1 (.in0(clk), .in1(bot2), .out(multiplexer_1_out), .sel(mudar));
  or or_1 (or_1_out, mudar, counter_2_carry);
  Counter #(.width(4), .max('h9)) counter_2 (
    .Q(out_7), .carry(counter_2_carry), .clk(multiplexer_2_out), .clr(reset), .down(1'b1));  // open: load, D, count, preset
  Multiplexer #(.enable("false")) multiplexer_2 (.in0(clk), .in1(bot1), .out(multiplexer_2_out), .sel(mudar));
endmodule

module tempo_minutos (
  input  _2,
  input  _1,
  input  reset,
  input  bot2,
  input  bot1,
  input  clk,
  input  mudar,
  output [3:0] out_8,
  output [3:0] out_9
);

  wire and_1_out, and_2_out, counter_2_carry, multiplexer_1_out, multiplexer_2_out, or_1_out, or_2_out;

  and and_1 (and_1_out, _1, ~mudar);  // AND_Gate
  and and_2 (and_2_out, _2, counter_2_carry);
  or or_1 (or_1_out, and_1_out, mudar);
  Counter #(.width(4), .max('h5)) counter_1 (
    .count(or_2_out), .Q(out_8), .clk(multiplexer_1_out), .clr(reset), .down(1'b1));  // open: load, D, carry, preset
  Multiplexer #(.enable("false")) multiplexer_1 (.in0(clk), .in1(bot2), .out(multiplexer_1_out), .sel(mudar));
  or or_2 (or_2_out, mudar, and_2_out);
  Counter #(.width(4), .max('h9)) counter_2 (
    .count(or_1_out), .Q(out_9), .carry(counter_2_carry), .clk(multiplexer_2_out), .clr(reset), .down(1'b1));  // open: load, D, preset
  Multiplexer #(.enable("false")) multiplexer_2 (.in0(clk), .in1(bot1), .out(multiplexer_2_out), .sel(mudar));
endmodule

module Alternar_jogador (
  input  troca,
  output clh1,
  output clk
);

  wire adder_1_out, clock_1_out, register_1_q;

  and and_1 (clk, clock_1_out, ~register_1_q);  // AND_Gate
  Clock clock_1 (.out(clock_1_out));
  Adder #(.width(1)) adder_1 (.a(1'b1), .b(register_1_q), .out(adder_1_out));  // open: cin, cout
  Register #(.width(1), .Select("low")) register_1 (.D(adder_1_out), .Q(register_1_q), .clk(troca));  // open: en, clr
  and and_2 (clh1, register_1_q, clock_1_out);
endmodule

module GTN_X (
  input  CONFIRMAR,
  input  NOVO,
  input  [3:0] X,
  input  [3:0] Y,
  output X_CERTO,
  output Y_CERTO,
  output SOMA_CERTA,
  output [7:0] vermelho,
  output [7:0] azul
);

  wire comparator_1_eq, comparator_2_eq, comparator_3_eq;
  wire [4:0] \diferença_1_out_3 , somador_1_out_3, somador_2_out_3;
  wire [7:0] bit_extender_1_out, cores_1_azul, cores_1_vermelho, random_1_out;

  Random random_1 (.clk(NOVO), .out(random_1_out));  // open: next, clr
  assign bit_extender_1_out = {{7{CONFIRMAR}}, CONFIRMAR};  // Bit_Extender bit_extender_1
  somador somador_1 (.in_1(random_1_out[7:4]), .in_2(random_1_out[3:0]), .out_3(somador_1_out_3));
  somador somador_2 (.in_1(Y), .in_2(X), .out_3(somador_2_out_3));
  and and_1 (X_CERTO, CONFIRMAR, comparator_1_eq);
  Comparator #(.width(4)) comparator_1 (.a(random_1_out[3:0]), .b(X), .eq(comparator_1_eq));  // open: gt, lt
  and and_2 (Y_CERTO, CONFIRMAR, comparator_2_eq);
  Comparator #(.width(4)) comparator_2 (.a(random_1_out[7:4]), .b(Y), .eq(comparator_2_eq));  // open: gt, lt
  and and_3 (SOMA_CERTA, CONFIRMAR, comparator_3_eq);
  Comparator #(.width(5)) comparator_3 (
    .a(somador_1_out_3), .b(somador_2_out_3), .eq(comparator_3_eq));  // open: gt, lt
  \diferença  \diferença_1  (.X(somador_1_out_3), .Y(somador_2_out_3), .out_3(\diferença_1_out_3 ));
  assign vermelho = bit_extender_1_out & cores_1_vermelho;  // AND_Gate and_4, 8 bits wide
  cores cores_1 (.vermelho(cores_1_vermelho), .azul(cores_1_azul), .in_1(\diferença_1_out_3 ));
  assign azul = cores_1_azul & bit_extender_1_out;  // AND_Gate and_5, 8 bits wide

  // Notes on the sheet:
  //   somador
  //   comparador de 4b
  //   comp. de 4b
  //   comp. de 5b
  //   diferença
  //   cores
endmodule

module somador (
  input  [3:0] in_1,
  input  [3:0] in_2,
  output [4:0] out_3
);

  Adder #(.width(4)) adder_1 (.a(in_1), .b(in_2), .out(out_3[3:0]), .cout(out_3[4]));  // open: cin
endmodule

module \diferença  (
  input  [4:0] X,
  input  [4:0] Y,
  output [4:0] out_3
);

  wire comparator_1_gt;

  Comparator #(.width(5)) comparator_1 (.a(X), .b(Y), .gt(comparator_1_gt));  // open: eq, lt
  Adder #(.width(5)) adder_1 (.a(X), .b(Y), .out(out_3), .cout(comparator_1_gt));  // open: cin
endmodule

module cores (
  input  [4:0] in_1,
  output [7:0] vermelho,
  output [7:0] azul
);

  assign vermelho = ~{in_1, 3'b111};  // NOT_Gate not_1, 8 bits wide

  assign azul = {in_1, 3'b111};
endmodule

// PALPITE A
module palpite_A (
  input  plus_A,
  input  C_V,
  input  AVAN,
  input  RESET,
  output [3:0] PALPITE,
  output [3:0] X,
  output X_JOGANDO,
  output [3:0] Y,
  output Y_JOGANDO,
  output JOGANDO_B,
  output RESET_2,
  output PASS,
  output CONF
);

  wire and_1_out, and_2_out, or_1_out;
  wire [1:0] counter_2_q;

  Counter #(.width(4), .max('hf)) counter_1 (
    .D(PALPITE), .Q(PALPITE), .clk(plus_A), .clr(AVAN));  // open: load, count, carry, preset, down
  or or_1 (or_1_out, RESET, JOGANDO_B);
  Counter #(.width(2), .max('h2)) counter_2 (
    .D(counter_2_q), .Q(counter_2_q), .clk(AVAN), .clr(or_1_out));  // open: load, count, carry, preset, down
  Comparator #(.width(2), .mode("unsigned")) comparator_1 (.a(counter_2_q), .b(2'b00), .eq(X_JOGANDO));  // open: gt, lt
  Comparator #(.width(2), .mode("unsigned")) comparator_2 (.a(counter_2_q), .b(2'b01), .eq(Y_JOGANDO));  // open: gt, lt
  Comparator #(.width(2), .mode("unsigned")) comparator_3 (.a(counter_2_q), .b(2'b10), .eq(JOGANDO_B));  // open: gt, lt
  and and_1 (and_1_out, X_JOGANDO, C_V);
  Register #(.width(4), .Select("low")) register_1 (.D(PALPITE), .Q(X), .clk(and_1_out), .clr(JOGANDO_B));  // open: en
  or or_2 (CONF, X_JOGANDO, Y_JOGANDO);
  Register #(.width(4), .Select("low")) register_2 (.D(PALPITE), .Q(Y), .clk(and_2_out), .clr(JOGANDO_B));  // open: en
  and and_2 (and_2_out, C_V, Y_JOGANDO);

  assign PASS = JOGANDO_B;
  assign RESET_2 = JOGANDO_B;

  // Other names for the same wires on the sheet: CA = X_JOGANDO; CB = Y_JOGANDO

  // Notes on the sheet:
  //   RESET: pull=down
  //   ESCOLHI X
  //   ESCOLHI Y
  //   CONFIRMEI
  //   MÁQUINA DE ESTADO
  //   1. ESCOLHI X
  //   2. ESCOLHI  Y
  //   3. CONFIRMEI
endmodule

// PALPITE B
module palpite_B (
  input  plus_B,
  input  C_V,
  input  AVAN,
  input  RESET,
  output [3:0] PALPITE,
  output [3:0] X,
  output X_JOGANDO,
  output [3:0] Y,
  output Y_JOGANDO,
  output JOGANDO_A,
  output RESET_2,
  output PASS,
  output CONF
);

  wire and_1_out, and_2_out, or_1_out;
  wire [1:0] counter_2_q;

  Counter #(.width(4), .max('hf)) counter_1 (
    .D(PALPITE), .Q(PALPITE), .clk(plus_B), .clr(AVAN));  // open: load, count, carry, preset, down
  or or_1 (or_1_out, RESET, JOGANDO_A);
  Counter #(.width(2), .max('h2)) counter_2 (
    .D(counter_2_q), .Q(counter_2_q), .clk(AVAN), .clr(or_1_out));  // open: load, count, carry, preset, down
  Comparator #(.width(2), .mode("unsigned")) comparator_1 (.a(counter_2_q), .b(2'b00), .eq(X_JOGANDO));  // open: gt, lt
  Comparator #(.width(2), .mode("unsigned")) comparator_2 (.a(counter_2_q), .b(2'b01), .eq(Y_JOGANDO));  // open: gt, lt
  Comparator #(.width(2), .mode("unsigned")) comparator_3 (.a(counter_2_q), .b(2'b10), .eq(JOGANDO_A));  // open: gt, lt
  and and_1 (and_1_out, X_JOGANDO, C_V);
  Register #(.width(4), .Select("low")) register_1 (.D(PALPITE), .Q(X), .clk(and_1_out), .clr(JOGANDO_A));  // open: en
  or or_2 (CONF, X_JOGANDO, Y_JOGANDO);
  Register #(.width(4), .Select("low")) register_2 (.D(PALPITE), .Q(Y), .clk(and_2_out), .clr(JOGANDO_A));  // open: en
  and and_2 (and_2_out, C_V, Y_JOGANDO);

  assign PASS = JOGANDO_A;
  assign RESET_2 = JOGANDO_A;

  // Other names for the same wires on the sheet: CA = X_JOGANDO; CB = Y_JOGANDO

  // Notes on the sheet:
  //   RESET: pull=down
  //   ESCOLHI X
  //   ESCOLHI Y
  //   CONFIRMEI
  //   MÁQUINA DE ESTADO
  //   1. ESCOLHI X
  //   2. ESCOLHI  Y
  //   3. CONFIRMEI
endmodule

// CORE
module core (
  input  NOVO_N,
  input  A,
  input  C_A,
  input  AVAN_A,
  input  C_B,
  input  B,
  input  AVAN_B,
  input  RESET,
  output [7:0] AZUL,
  output [7:0] VERMELHO,
  output SOMA_CERTA,
  output X_JOGANDO,
  output Y_JOGANDO,
  output [3:0] PONTO_A,
  output X_CERTO,
  output Y_CERTO,
  output FIM_A,
  output [3:0] PONTO_B,
  output FIM_B,
  output [3:0] X_ATUAL,
  output [3:0] Y_ATUAL,
  output JOGANDO_A,
  output JOGANDO_B,
  output [3:0] PALPITE_A,
  output [3:0] PALPITE_B
);

  wire and_1_out, and_2_out, and_3_out, and_4_out, and_5_out, and_6_out, and_7_out, and_8_out, and_9_out,
       and_10_out, and_11_out, GATILHO_A, GATILHO_B, or_1_out, tunel_C, tunel_CA, tunel_CB, tunel_JOG_X_A,
       tunel_JOG_X_B, tunel_JOG_Y_A, tunel_JOG_Y_B, tunnel;
  wire [3:0] tunel_XA, tunel_XB, tunel_YA, tunel_YB;

  and and_1 (and_1_out, C_A, JOGANDO_A);
  and and_2 (and_2_out, JOGANDO_A, AVAN_A);
  and and_3 (and_3_out, C_B, JOGANDO_B);
  and and_4 (and_4_out, JOGANDO_B, AVAN_B);
  or or_1 (or_1_out, GATILHO_A, GATILHO_B);
  palpite_A palpite_a_1 (
    .PALPITE(PALPITE_A), .X(tunel_XA), .X_JOGANDO(tunel_JOG_X_A), .plus_A(A), .Y(tunel_YA),
    .Y_JOGANDO(tunel_JOG_Y_A), .C_V(and_1_out), .AVAN(and_2_out), .JOGANDO_B(GATILHO_A), .RESET(RESET),
    .CONF(tunel_CA));  // open: RESET_2, PASS
  palpite_B palpite_b_1 (
    .PALPITE(PALPITE_B), .X(tunel_XB), .X_JOGANDO(tunel_JOG_X_B), .plus_B(B), .Y(tunel_YB),
    .Y_JOGANDO(tunel_JOG_Y_B), .C_V(and_3_out), .AVAN(and_4_out), .JOGANDO_A(GATILHO_B), .RESET(RESET),
    .CONF(tunel_CB));  // open: RESET_2, PASS
  T_Flip_Flop t_ff_1 (.clk(or_1_out), .T(1'b1), .Q(JOGANDO_B), .Qn(JOGANDO_A));  // open: preset, reset
  or or_2 (X_JOGANDO, and_5_out, and_6_out);
  and and_5 (and_5_out, tunel_JOG_X_A, JOGANDO_A);
  and and_6 (and_6_out, tunel_JOG_X_B, JOGANDO_B);
  or or_3 (tunel_C, tunel_CA, tunel_CB);
  or or_4 (Y_JOGANDO, and_8_out, and_7_out);
  and and_7 (and_7_out, tunel_JOG_Y_A, JOGANDO_A);
  and and_8 (and_8_out, tunel_JOG_Y_B, JOGANDO_B);
  Multiplexer #(.width(4), .enable("false")) multiplexer_1 (
    .in0(tunel_XA), .in1(tunel_XB), .out(X_ATUAL), .sel(JOGANDO_B));
  Multiplexer #(.width(4), .enable("false")) multiplexer_2 (
    .in0(tunel_YA), .in1(tunel_YB), .out(Y_ATUAL), .sel(JOGANDO_B));
  GTN_X gtn_x_1 (
    .CONFIRMAR(tunel_C), .NOVO(NOVO_N), .X(X_ATUAL), .Y(Y_ATUAL), .X_CERTO(X_CERTO), .Y_CERTO(Y_CERTO),
    .SOMA_CERTA(SOMA_CERTA), .vermelho(VERMELHO), .azul(AZUL));
  and and_9 (and_9_out, X_CERTO, Y_CERTO);
  Counter #(.width(1), .max('h1)) counter_1 (
    .Q(tunnel), .clk(and_9_out), .clr(tunnel));  // open: load, D, count, carry, preset, down
  and and_10 (and_10_out, tunnel, JOGANDO_A);
  and and_11 (and_11_out, tunnel, JOGANDO_B);
  Counter #(.width(4), .max('h4)) counter_2 (
    .Q(PONTO_A), .carry(FIM_A), .clk(and_10_out));  // open: load, D, count, clr, preset, down
  Counter #(.width(4), .max('h4)) counter_3 (
    .Q(PONTO_B), .carry(FIM_B), .clk(and_11_out));  // open: load, D, count, clr, preset, down

  // Other names for the same wires on the sheet: tunel_C_A[3:0] = PALPITE_A; tunel_C_B[3:0] = PALPITE_B;
  //   tunel_N = NOVO_N; tunel_R = RESET
endmodule
